// Logisim project alu.circ as structural Verilog: 1 circuit, main circuit alu
module alu (
  input  [31:0] A,
  input  [31:0] B,
  input  [3:0] ALUSel,
  output [31:0] Result
);

  wire not_2_out;
  wire [31:0] add0, and1, not4, or2, sll6, slt7, sra5, sub8, xor3;

  Adder #(.width(32)) adder_1 (.a(A), .b(B), .out(add0));  // open: cin, cout
  assign and1 = A & B;  // AND_Gate and_1, 32 bits wide
  assign or2 = A | B;  // OR_Gate or_1, 32 bits wide
  assign xor3 = A ^ B;  // XOR_Gate xor_1, 32 bits wide
  assign not4 = ~A;  // NOT_Gate not_1, 32 bits wide
  Shifter #(.width(32), .shift("lr")) shifter_1 (.in(A), .\dist (B[4:0]), .out(sra5));
  Shifter #(.width(32)) shifter_2 (.in(A), .\dist (B[4:0]), .out(sll6));
  Subtractor #(.width(32)) subtractor_1 (.a(A), .b(B), .out(sub8));  // open: bin, bout
  not not_2 (not_2_out, sub8[31]);
  assign slt7 = {{31{not_2_out}}, not_2_out};  // Bit_Extender bit_extender_1
  Multiplexer #(.select(4), .width(32), .enable("false")) multiplexer_1 (
    .in0(add0), .in1(and1), .in2(or2), .in3(xor3), .in4(not4), .in5(sra5), .in6(sll6), .in7(slt7),
    .in8(sub8), .out(Result));  // open: in9, in10, in11, in12, in13, in14, in15, sel

  // Notes on the sheet:
  //   INPUTS to your circuit
  //   DON'T CHANGE THE LOCATIONS OF THE INPUTS AND OUTPUTS!
  //   OUTPUT from your circuit
endmodule
